// Logisim project cpu.circ as structural Verilog: 2 circuits, main circuit main
module main (
  input  [31:0] INSTRUCTION,
  input  CLOCK,
  output [31:0] PROGRAM_COUNTER,
  output [31:0] ra,
  output [31:0] sp,
  output [31:0] t0,
  output [31:0] t1,
  output [31:0] t2,
  output [31:0] s0,
  output [31:0] s1,
  output [31:0] a0
);

  wire AddrSel, ASel, BrEq, BrLt, BrSel, BrUn, BSel, MemRW, PCSel, RegWEn;
  wire [1:0] WBSel;
  wire [2:0] ImmSel;
  wire [3:0] ALUSel;
  wire [31:0] DMEM_output, Imm, INSTRUCTION_Q, multiplexer_1_out, multiplexer_2_out, multiplexer_3_out,
       multiplexer_4_out, multiplexer_5_out, PC_plus_4, PC_VALUE, PC_VALUE_plus_4, ReadData, Result, rs1,
       rs2, wb, WriteAddr;

  Multiplexer #(.width(32), .enable("false")) multiplexer_1 (
    .in0(PC_plus_4), .in1(Result), .out(multiplexer_1_out), .sel(PCSel));
  control_logic control_logic_1 (
    .BSel(BSel), .BrUn(BrUn), .PCSel(PCSel), .RegWEn(RegWEn), .ImmSel(ImmSel), .BrLt(BrLt), .ASel(ASel),
    .BrEq(BrEq), .inst(INSTRUCTION_Q), .ALUSel(ALUSel), .MemRW(MemRW), .WBSel(WBSel), .AddrSel(AddrSel),
    .BrSel(BrSel));
  Adder #(.width(32)) adder_1 (.a(PROGRAM_COUNTER), .b(32'h4), .out(PC_plus_4));  // open: cin, cout
  Register #(.width(32)) PC (.D(multiplexer_1_out), .clk(CLOCK), .Q(PROGRAM_COUNTER));  // open: en, clr
  Register #(.width(32)) register_1 (.D(PROGRAM_COUNTER), .clk(CLOCK), .Q(PC_VALUE));  // open: en, clr
  Adder #(.width(32)) adder_2 (.a(PC_VALUE), .b(32'h4), .out(PC_VALUE_plus_4));  // open: cin, cout
  Multiplexer #(.width(32), .enable("false")) multiplexer_2 (
    .in0(INSTRUCTION), .in1(32'h13), .out(multiplexer_2_out), .sel(PCSel));
  imm_gen imm_gen_1 (.ImmSel(ImmSel), .inst(INSTRUCTION_Q), .imm(Imm));
  Register #(.width(32)) register_2 (.D(multiplexer_2_out), .clk(CLOCK), .Q(INSTRUCTION_Q));  // open: en, clr
  regfile_main RegFile (
    .rs2(INSTRUCTION_Q[24:20]), .rd(INSTRUCTION_Q[11:7]), .Read_Data_1(rs1), .Read_Data_2(rs2), .ra(ra),
    .sp(sp), .t0(t0), .t1(t1), .t2(t2), .s0(s0), .s1(s1), .a0(a0), .rs1(INSTRUCTION_Q[19:15]),
    .Write_Data(wb), .RegWEn(RegWEn), .clk(CLOCK));
  Multiplexer #(.width(32), .enable("false")) multiplexer_3 (
    .in0(rs2), .in1(Imm), .out(multiplexer_3_out), .sel(BrSel));
  Multiplexer #(.width(32), .enable("false")) multiplexer_4 (
    .in0(rs1), .in1(PC_VALUE), .out(multiplexer_4_out), .sel(ASel));
  Multiplexer #(.width(32), .enable("false")) multiplexer_5 (.in0(rs2), .in1(Imm), .out(multiplexer_5_out), .sel(BSel));
  alu Arithmetic_Logic_Unit (.ALUSel(ALUSel), .Result(Result), .A(multiplexer_4_out), .B(multiplexer_5_out));
  branch_comp branch_comp_1 (.BrEq(BrEq), .BrUn(BrUn), .rs1(rs1), .BrLt(BrLt), .rs2(multiplexer_3_out));
  Multiplexer #(.width(32), .enable("false")) multiplexer_6 (.in0(Result), .in1(rs1), .out(WriteAddr), .sel(AddrSel));
  // mem_main DMEM: pin names not known; wires that end beside it: WriteAddr, rs2, CLOCK, MemRW, DMEM_output
  after_DMEM after_dmem_1 (
    .Addr(Result), .funct3(INSTRUCTION_Q[14:12]), .DMEM_output(DMEM_output), .real_output(ReadData));
  Multiplexer #(.select(2), .width(32), .enable("false")) multiplexer_7 (
    .in0(ReadData), .in1(Result), .in2(PC_VALUE_plus_4), .in3(Imm), .out(wb), .sel(WBSel));

  // Other names for the same wires on the sheet: clk = CLOCK

  // Notes on the sheet:
  //   Output
  //   IMEM (do **NOT** move this)
  //   Inputs
  //   It is OK to move the PC, RegFile, ALU, MEM, Branch Comp, Imm Gen, and Control Logic to wherever is most convenient for you when constructing your CPU, and to delete this text
  //   Inputs/Outputs for testing. Do **NOT** move these.
endmodule

module after_DMEM (
  input  [31:0] Addr,
  input  [2:0] funct3,
  input  [31:0] DMEM_output,
  output [31:0] real_output
);

  wire [31:0] lb, lh;

  Multiplexer #(.select(2), .width(32), .enable("false")) multiplexer_1 (
    .in0({{25{DMEM_output[7]}}, DMEM_output[6:0]}), .in1({{25{DMEM_output[15]}}, DMEM_output[14:8]}),
    .in2({{25{DMEM_output[23]}}, DMEM_output[22:16]}), .in3({{25{DMEM_output[31]}}, DMEM_output[30:24]}),
    .out(lb), .sel(Addr[1:0]));
  Multiplexer #(.width(32), .enable("false")) multiplexer_2 (
    .in0({{17{DMEM_output[15]}}, DMEM_output[14:0]}), .in1({{17{DMEM_output[31]}}, DMEM_output[30:16]}),
    .out(lh), .sel(Addr[1]));
  Multiplexer #(.select(3), .width(32), .enable("false")) multiplexer_3 (
    .in0(lb), .in1(lh), .in2(DMEM_output), .out(real_output), .sel(funct3));  // open: in3, in4, in5, in6, in7

  // Other names for the same wires on the sheet: byte0[31:0] = {{25{DMEM_output[7]}}, DMEM_output[6:0]};
  //   half0[31:0] = {{17{DMEM_output[15]}}, DMEM_output[14:0]}; lw[31:0] = DMEM_output;
  //   byte1[31:0] = {{25{DMEM_output[15]}}, DMEM_output[14:8]};
  //   byte2[31:0] = {{25{DMEM_output[23]}}, DMEM_output[22:16]};
  //   half1[31:0] = {{17{DMEM_output[31]}}, DMEM_output[30:16]};
  //   byte3[31:0] = {{25{DMEM_output[31]}}, DMEM_output[30:24]}
endmodule
